// Logisim project alu.circ as structural Verilog: 8 circuits, main circuit ALU
module ALU (
  input  [31:0] X,
  input  [31:0] Y,
  input  [3:0] AluOP,
  output Signed_Overflow,
  output UnSigned_Overflow,
  output Equal,
  output [31:0] Result,
  output [31:0] Result_2
);

  wire adder_1_cout, subtractor_1_bout;
  wire [0:0] comparator_1_lt, comparator_2_lt;
  wire [1:0] adder_2_cout, subtractor_2_bout;
  wire [30:0] adder_1_out, subtractor_1_out;
  wire [31:0] and_1_out, divider_1_out, divider_1_rem, multiplier_1_cout, multiplier_1_out, not_1_out,
       or_1_out, or_2_out, shifter_1_out, shifter_2_out, shifter_3_out, xor_1_out;
  wire [31:31] adder_2_out, subtractor_2_out;

  // Probe on X
  // Probe on X
  // Probe on Y
  // Probe on Y
  Multiplier #(.width(32)) multiplier_1 (.a(X), .b(Y), .out(multiplier_1_out), .cout(multiplier_1_cout));  // open: cin
  Divider #(.width(32)) divider_1 (.a(X), .b(Y), .out(divider_1_out), .rem(divider_1_rem));  // open: upper
  Adder #(.width(31)) adder_1 (.a(X[30:0]), .b(Y[30:0]), .out(adder_1_out), .cout(adder_1_cout));  // open: cin
  Adder #(.width(1)) adder_2 (.a(X[31]), .b(Y[31]), .out(adder_2_out[31]), .cin(adder_1_cout), .cout(adder_2_cout[0]));
  assign and_1_out = X & Y;  // AND_Gate and_1, 32 bits wide
  assign or_1_out = X | Y;  // OR_Gate or_1, 32 bits wide
  assign xor_1_out = X ^ Y;  // XOR_Gate xor_1, 32 bits wide
  assign or_2_out = X | Y;  // OR_Gate or_2, 32 bits wide
  Comparator #(.width(32)) comparator_1 (.a(X), .b(Y), .lt(comparator_1_lt[0]));  // open: gt, eq
  Comparator #(.width(32), .mode("unsigned")) comparator_2 (
    .a(X), .b(Y), .eq(Equal), .lt(comparator_2_lt[0]));  // open: gt
  // Probe on AluOP
  Subtractor #(.width(31)) subtractor_1 (
    .a(X[30:0]), .b(Y[30:0]), .out(subtractor_1_out), .bout(subtractor_1_bout));  // open: bin
  Subtractor #(.width(1)) subtractor_2 (
    .a(X[31]), .b(Y[31]), .out(subtractor_2_out[31]), .bin(subtractor_1_bout), .bout(subtractor_2_bout[0]));
  assign not_1_out = ~or_2_out;  // NOT_Gate not_1, 32 bits wide
  // Probe on Result
  // Probe on Result
  Shifter #(.width(32)) shifter_1 (.in(X), .\dist (Y[4:0]), .out(shifter_1_out));
  Shifter #(.width(32), .shift("ar")) shifter_2 (.in(X), .\dist (Y[4:0]), .out(shifter_2_out));
  Shifter #(.width(32), .shift("lr")) shifter_3 (.in(X), .\dist (Y[4:0]), .out(shifter_3_out));
  xor xor_2 (adder_2_cout[1], adder_1_cout, adder_2_cout[0]);
  xor xor_3 (subtractor_2_bout[1], subtractor_1_bout, subtractor_2_bout[0]);
  // Probe on Result_2
  Multiplexer #(.select(4), .width(32), .enable("false")) multiplexer_1 (
    .in0(shifter_1_out), .in1(shifter_2_out), .in2(shifter_3_out), .in3(multiplier_1_out),
    .in4(divider_1_out), .in5({adder_2_out[31], adder_1_out}),
    .in6({subtractor_2_out[31], subtractor_1_out}), .in7(and_1_out), .in8(or_1_out), .in9(xor_1_out),
    .in10(not_1_out), .in11({{31{1'b0}}, comparator_1_lt[0]}), .in12({{31{1'b0}}, comparator_2_lt[0]}),
    .in13({32{1'b0}}), .in14({32{1'b0}}), .in15({32{1'b0}}), .out(Result), .sel(AluOP));
  Multiplexer #(.select(4), .width(32), .enable("false")) multiplexer_2 (
    .in0({32{1'b0}}), .in1({32{1'b0}}), .in2({32{1'b0}}), .in3(multiplier_1_cout), .in4(divider_1_rem),
    .in5({32{1'b0}}), .in6({32{1'b0}}), .in7({32{1'b0}}), .in8({32{1'b0}}), .in9({32{1'b0}}),
    .in10({32{1'b0}}), .in11({32{1'b0}}), .in12({32{1'b0}}), .in13({32{1'b0}}), .in14({32{1'b0}}),
    .in15({32{1'b0}}), .out(Result_2), .sel(AluOP));
  Multiplexer #(.select(4), .width(2), .enable("false")) multiplexer_3 (
    .in0(2'b00), .in1(2'b00), .in2(2'b00), .in3(2'b00), .in4(2'b00), .in5(adder_2_cout),
    .in6(subtractor_2_bout), .in7(2'b00), .in8(2'b00), .in9(2'b00), .in10(2'b00), .in11(2'b00), .in12(2'b00),
    .in13(2'b00), .in14(2'b00), .in15(2'b00), .out({Signed_Overflow, UnSigned_Overflow}), .sel(AluOP));

  // Other names for the same wires on the sheet: CF = UnSigned_Overflow; OF = Signed_Overflow;
  //   Result2[31:0] = Result_2; S[3:0] = AluOP

  // Notes on the sheet:
  //   不要改变此引脚区域内容，也不要改变ALU封装形式
  //   输入引脚
  //   请在下方利用上方输入输出引脚的隧道信号构建ALU电路，ctrl+d复制选择部件
  //   输出引脚
  //   探测区域
endmodule

module \演示电路  (
  input  [31:0] X,
  input  [31:0] Y,
  input  [3:0] ALUOP,
  output Signed_Overflow,
  output Unsigned_overflow,
  output [31:0] Result,
  output [31:0] Result_2,
  output Equal
);

  // Probe on X
  // Probe on X
  ALU alu_1 (
    .AluOP(ALUOP), .X(X), .Equal(Equal), .Result(Result), .Signed_Overflow(Signed_Overflow), .Y(Y),
    .Result_2(Result_2), .UnSigned_Overflow(Unsigned_overflow));
  // Probe on ALUOP
  // Probe on Y
  // Probe on Y
  // Probe on Result
  // Probe on Result
  // Probe on Result_2
endmodule

module \毛刺现象  (
  input  in_1
);

  wire and_1_out, not_1_out;

  not not_1 (not_1_out, in_1);
  and and_1 (and_1_out, in_1, not_1_out);
  Counter counter_1 (.clk(and_1_out));  // open: load, D, count, Q, carry, clr

  // Notes on the sheet:
  //   尝试反复点击输入引脚改变值，观察计算器的变化
  //   逻辑上应该为零，但计数器观察到了跳变
endmodule

module \震荡电路  (
  input  in_1,
  output out_2
);

  nand nand_1 (out_2, in_1, out_2);

  // Notes on the sheet:
  //   尝试修改输入引脚的电平,输入输出存在反馈，导致电路状态不稳定
  //   如出现类似情况，尝试去掉部分回路连接直至故障消除
  //   华中科技大学计算机学院 计算机组成原理
endmodule

module \信号冲突  (
  input  in_1,
  input  in_2,
  output out_3
);


  assign in_2 = in_1;
  assign out_3 = in_1;

  // Notes on the sheet:
  //   输入相同时无问题，不同时出错，红色显示
  //   华中科技大学计算机学院 计算机组成原理
endmodule

module \不同颜色信号线  (
  input  \引脚类型不对 ,
  input  [1:0] in_2,
  input  in_3
);

  wire undriven;
  wire [1:0] nand_2_out, undriven_3;
  wire [1:1] undriven_2;

  nand nand_1 (\引脚类型不对 , 1'b1, 1'b0, undriven, 1'b1);
  assign nand_2_out = ~(in_2 & undriven_3 & {undriven_2[1], in_3});  // NAND_Gate nand_2, 2 bits wide
  // Pins of 1 and 2 bits meet at {undriven_2[1], in_3}

  // Notes on the sheet:
  //   深绿色表示低电平
  //   蓝色表示未知状态
  //   灰色表示飞线
  //   亮绿色表示高电平
  //   红色表示信号冲突
  //   黑色表示多位总线
  //   橙色表示位宽不匹配
  //   华中科技大学计算机学院 计算机组成原理
endmodule

module \分线器使用  (
  input  [7:0] in_1
);


  // Notes on the sheet:
  //   分线器使用方法
  //   8分3，两个3位，一个2位
  //   分线器不分输入输出，可反向使用进行线缆汇总
  //   华中科技大学计算机学院 计算机组成原理
  //   8分二，高位在下
  //   8分二，高位在上
  //   只分部分位，位宽不对称
  //   只分1位，如取符号位
  //   8分8
endmodule

module \等差数列求和  (
  input  [31:0] \等差值 ,
  input  [31:0] \初始值 ,
  input  in_3
);

  wire clock_1_out, comparator_1_eq, comparator_2_eq, not_1_out, not_2_out, or_1_out;
  wire [31:0] alu_1_result, alu_2_result, counter_1_q, multiplexer_1_out, multiplexer_2_out, register_1_q,
       register_2_q;

  Counter #(.width(32), .max('hffffffff)) counter_1 (
    .Q(counter_1_q), .clk(clock_1_out), .clr(in_3));  // open: load, D, count, carry
  // Probe on \等差值 
  // Probe on \初始值 
  Comparator #(.width(32)) comparator_1 (.a(32'h1), .b(counter_1_q), .eq(comparator_1_eq));  // open: gt, lt
  Comparator #(.width(32)) comparator_2 (.a(counter_1_q), .b({32{1'b0}}), .eq(comparator_2_eq));  // open: gt, lt
  Multiplexer #(.width(32), .enable("false")) multiplexer_1 (
    .in0({32{1'b0}}), .in1(\等差值 ), .out(multiplexer_1_out), .sel(not_1_out));
  not not_1 (not_1_out, or_1_out);
  or or_1 (or_1_out, comparator_1_eq, comparator_2_eq);
  Register #(.width(32)) register_1 (
    .D(multiplexer_2_out), .Q(register_1_q), .clk(clock_1_out), .clr(in_3));  // open: en
  Multiplexer #(.width(32), .enable("false")) multiplexer_2 (
    .in0(\初始值 ), .in1(alu_1_result), .out(multiplexer_2_out), .sel(not_2_out));
  not not_2 (not_2_out, comparator_2_eq);
  Clock clock_1 (.out(clock_1_out));
  ALU alu_1 (
    .AluOP(4'b0101), .X(multiplexer_1_out), .Result(alu_1_result), .Y(register_1_q));  // open: Equal, Signed_Overflow, Result_2, UnSigned_Overflow
  Hex_Digit_Display hex_digit_display_1 (.value(alu_2_result[31:28]));  // open: dp
  Register #(.width(32)) register_2 (.D(alu_2_result), .Q(register_2_q), .clk(clock_1_out), .clr(in_3));  // open: en
  Hex_Digit_Display hex_digit_display_2 (.value(alu_2_result[23:20]));  // open: dp
  Hex_Digit_Display hex_digit_display_3 (.value(alu_2_result[27:24]));  // open: dp
  ALU alu_2 (
    .AluOP(4'b0101), .X(alu_1_result), .Result(alu_2_result), .Y(register_2_q));  // open: Equal, Signed_Overflow, Result_2, UnSigned_Overflow
  Hex_Digit_Display hex_digit_display_4 (.value(alu_2_result[15:12]));  // open: dp
  Hex_Digit_Display hex_digit_display_5 (.value(alu_2_result[19:16]));  // open: dp
  Hex_Digit_Display hex_digit_display_6 (.value(alu_2_result[11:8]));  // open: dp
  Hex_Digit_Display hex_digit_display_7 (.value(alu_2_result[7:4]));  // open: dp
  // Probe on alu_2_result
  Hex_Digit_Display hex_digit_display_8 (.value(alu_2_result[3:0]));  // open: dp
endmodule
