// Logisim project regfile.circ as structural Verilog: 2 circuits, main circuit regfile
module regfile (
  input  [4:0] Reg1_num,
  input  [4:0] Reg2,
  input  [4:0] Write_Reg_num,
  input  [31:0] Din,
  input  Write_Enable,
  input  Clock,
  output [31:0] Reg1,
  output [31:0] s0_Value,
  output [31:0] s1_Value,
  output [31:0] s2_Value,
  output [31:0] ra_Value,
  output [31:0] Reg2_2
);

  wire [7:0] demultiplexer_1_out0, demultiplexer_1_out8, demultiplexer_1_out16, demultiplexer_1_out24;
  wire [31:0] _0_q, _1_q, _2_q, _3_q, _4_q, _5_q, _6_q, _7_q, _8_q, _9_q, _10_q, _11_q, _12_q, _13_q, _14_q,
       _15_q, _19_q, _20_q, _21_q, _22_q, _23_q, _24_q, _25_q, _26_q, _27_q, _28_q, _29_q, _30_q;

  Demultiplexer #(.select(5), .enable("false")) demultiplexer_1 (
    .out0(demultiplexer_1_out0[0]), .out1(demultiplexer_1_out0[1]), .out2(demultiplexer_1_out0[2]),
    .out3(demultiplexer_1_out0[3]), .out4(demultiplexer_1_out0[4]), .out5(demultiplexer_1_out0[5]),
    .out6(demultiplexer_1_out0[6]), .out7(demultiplexer_1_out0[7]), .out8(demultiplexer_1_out8[0]),
    .out9(demultiplexer_1_out8[1]), .out10(demultiplexer_1_out8[2]), .out11(demultiplexer_1_out8[3]),
    .out12(demultiplexer_1_out8[4]), .out13(demultiplexer_1_out8[5]), .out14(demultiplexer_1_out8[6]),
    .out15(demultiplexer_1_out8[7]), .out16(demultiplexer_1_out16[0]), .out17(demultiplexer_1_out16[1]),
    .out18(demultiplexer_1_out16[2]), .out19(demultiplexer_1_out16[3]), .out20(demultiplexer_1_out16[4]),
    .out21(demultiplexer_1_out16[5]), .out22(demultiplexer_1_out16[6]), .out23(demultiplexer_1_out16[7]),
    .out24(demultiplexer_1_out24[0]), .out25(demultiplexer_1_out24[1]), .out26(demultiplexer_1_out24[2]),
    .out27(demultiplexer_1_out24[3]), .out28(demultiplexer_1_out24[4]), .out29(demultiplexer_1_out24[5]),
    .out30(demultiplexer_1_out24[6]), .out31(demultiplexer_1_out24[7]), .in(Write_Enable), .sel(Write_Reg_num));
  Register #(.width(32)) _0 (.D(Din), .en(1'b0), .Q(_0_q), .clk(Clock), .clr(1'b1));
  Register #(.width(32)) _8 (.D(Din), .en(demultiplexer_1_out8[0]), .Q(_8_q), .clk(Clock));  // open: clr
  Register #(.width(32)) _16 (.D(Din), .en(demultiplexer_1_out16[0]), .Q(s0_Value), .clk(Clock));  // open: clr
  Register #(.width(32)) _24 (.D(Din), .en(demultiplexer_1_out24[0]), .Q(_24_q), .clk(Clock));  // open: clr
  Register #(.width(32)) _1 (.D(Din), .en(demultiplexer_1_out0[1]), .Q(_1_q), .clk(Clock));  // open: clr
  Register #(.width(32)) _9 (.D(Din), .en(demultiplexer_1_out8[1]), .Q(_9_q), .clk(Clock));  // open: clr
  Register #(.width(32)) _17 (.D(Din), .en(demultiplexer_1_out16[1]), .Q(s1_Value), .clk(Clock));  // open: clr
  Register #(.width(32)) _25 (.D(Din), .en(demultiplexer_1_out24[1]), .Q(_25_q), .clk(Clock));  // open: clr
  Register #(.width(32)) _2 (.D(Din), .en(demultiplexer_1_out0[2]), .Q(_2_q), .clk(Clock));  // open: clr
  Register #(.width(32)) _10 (.D(Din), .en(demultiplexer_1_out8[2]), .Q(_10_q), .clk(Clock));  // open: clr
  Register #(.width(32)) _18 (.D(Din), .en(demultiplexer_1_out16[2]), .Q(s2_Value), .clk(Clock));  // open: clr
  Register #(.width(32)) _26 (.D(Din), .en(demultiplexer_1_out24[2]), .Q(_26_q), .clk(Clock));  // open: clr
  Register #(.width(32)) _3 (.D(Din), .en(demultiplexer_1_out0[3]), .Q(_3_q), .clk(Clock));  // open: clr
  Register #(.width(32)) _11 (.D(Din), .en(demultiplexer_1_out8[3]), .Q(_11_q), .clk(Clock));  // open: clr
  Register #(.width(32)) _19 (.D(Din), .en(demultiplexer_1_out16[3]), .Q(_19_q), .clk(Clock));  // open: clr
  Register #(.width(32)) _27 (.D(Din), .en(demultiplexer_1_out24[3]), .Q(_27_q), .clk(Clock));  // open: clr
  Register #(.width(32)) _4 (.D(Din), .en(demultiplexer_1_out0[4]), .Q(_4_q), .clk(Clock));  // open: clr
  Register #(.width(32)) _12 (.D(Din), .en(demultiplexer_1_out8[4]), .Q(_12_q), .clk(Clock));  // open: clr
  Register #(.width(32)) _20 (.D(Din), .en(demultiplexer_1_out16[4]), .Q(_20_q), .clk(Clock));  // open: clr
  Register #(.width(32)) _28 (.D(Din), .en(demultiplexer_1_out24[4]), .Q(_28_q), .clk(Clock));  // open: clr
  Register #(.width(32)) _6 (.D(Din), .en(demultiplexer_1_out0[6]), .Q(_6_q), .clk(Clock));  // open: clr
  Register #(.width(32)) _5 (.D(Din), .en(demultiplexer_1_out0[5]), .Q(_5_q), .clk(Clock));  // open: clr
  Register #(.width(32)) _14 (.D(Din), .en(demultiplexer_1_out8[6]), .Q(_14_q), .clk(Clock));  // open: clr
  Register #(.width(32)) _13 (.D(Din), .en(demultiplexer_1_out8[5]), .Q(_13_q), .clk(Clock));  // open: clr
  Register #(.width(32)) _22 (.D(Din), .en(demultiplexer_1_out16[6]), .Q(_22_q), .clk(Clock));  // open: clr
  Register #(.width(32)) _21 (.D(Din), .en(demultiplexer_1_out16[5]), .Q(_21_q), .clk(Clock));  // open: clr
  Register #(.width(32)) _29 (.D(Din), .en(demultiplexer_1_out24[5]), .Q(_29_q), .clk(Clock));  // open: clr
  Register #(.width(32)) _30 (.D(Din), .en(demultiplexer_1_out24[6]), .Q(_30_q), .clk(Clock));  // open: clr
  Register #(.width(32)) _7 (.D(Din), .en(demultiplexer_1_out0[7]), .Q(_7_q), .clk(Clock));  // open: clr
  Register #(.width(32)) _15 (.D(Din), .en(demultiplexer_1_out8[7]), .Q(_15_q), .clk(Clock));  // open: clr
  Register #(.width(32)) _23 (.D(Din), .en(demultiplexer_1_out16[7]), .Q(_23_q), .clk(Clock));  // open: clr
  Register #(.width(32)) _31 (.D(Din), .en(demultiplexer_1_out24[7]), .Q(ra_Value), .clk(Clock));  // open: clr
  Multiplexer #(.select(5), .width(32), .enable("false")) multiplexer_1 (
    .in0(_0_q), .in1(_1_q), .in2(_2_q), .in3(_3_q), .in4(_4_q), .in5(_5_q), .in6(_6_q), .in7(_7_q),
    .in8(_8_q), .in9(_9_q), .in10(_10_q), .in11(_11_q), .in12(_12_q), .in13(_13_q), .in14(_14_q),
    .in15(_15_q), .in16(s0_Value), .in17(s1_Value), .in18(s2_Value), .in19(_19_q), .in20(_20_q),
    .in21(_21_q), .in22(_22_q), .in23(_23_q), .in24(_24_q), .in25(_25_q), .in26(_26_q), .in27(_27_q),
    .in28(_28_q), .in29(_29_q), .in30(_30_q), .in31(ra_Value), .out(Reg1), .sel(Reg1_num));
  Multiplexer #(.select(5), .width(32), .enable("false")) multiplexer_2 (
    .in0(_0_q), .in1(_1_q), .in2(_2_q), .in3(_3_q), .in4(_4_q), .in5(_5_q), .in6(_6_q), .in7(_7_q),
    .in8(_8_q), .in9(_9_q), .in10(_10_q), .in11(_11_q), .in12(_12_q), .in13(_13_q), .in14(_14_q),
    .in15(_15_q), .in16(s0_Value), .in17(s1_Value), .in18(s2_Value), .in19(_19_q), .in20(_20_q),
    .in21(_21_q), .in22(_22_q), .in23(_23_q), .in24(_24_q), .in25(_25_q), .in26(_26_q), .in27(_27_q),
    .in28(_28_q), .in29(_29_q), .in30(_30_q), .in31(ra_Value), .out(Reg2_2), .sel(Reg2));

  // Other names for the same wires on the sheet: clk = Clock; ra[31:0] = ra_Value; reg2_num[4:0] = Reg2;
  //   reg2_t[31:0] = Reg2_2; s0[31:0] = s0_Value; s1[31:0] = s1_Value; s2[31:0] = s2_Value; WE = Write_Enable;
  //   write_data[31:0] = Din

  // Notes on the sheet:
  //   输入引脚
  //   输出引脚
  //   请在下方利用上方输入输出引脚的隧道信号构建ALU电路，ctrl+d复制选择部件
  //   Debug引脚，便于观测寄存器值
  //   请勿修改引脚以及封装，直接使用隧道连接电路
endmodule

module accumulator (
  input  in_1,
  input  in_2
);

  wire clock_1_out, comparator_1_gt, comparator_2_gt, comparator_3_lt, comparator_4_gt, not_1_out, not_2_out;
  wire [4:0] adder_1_out, \存入_读取地址 ;
  wire [31:0] alu_1_p4, alu_2_p4, counter_1_q, multiplexer_1_out, multiplexer_2_out, ram_1_data,
       register_1_q, \累加中间结果 , \累加单项 ;

  // Probe on \存入_读取地址 
  Counter #(.width(32), .max('hffffffff)) counter_1 (
    .count(1'b1), .Q(counter_1_q), .clk(clock_1_out), .clr(in_2));  // open: load, D, carry
  // Probe on \累加单项 
  Comparator #(.width(32)) comparator_1 (.a(32'hf), .b(alu_1_p4), .gt(comparator_1_gt));  // open: eq, lt
  Multiplexer #(.width(32), .enable("false")) multiplexer_1 (
    .in0({32{1'b0}}), .in1(32'h1), .out(multiplexer_1_out), .sel(comparator_2_gt));
  Comparator #(.width(32)) comparator_2 (.a(counter_1_q), .b(32'h1), .gt(comparator_2_gt));  // open: eq, lt
  Register #(.width(32)) register_1 (
    .D(alu_1_p4), .en(comparator_1_gt), .Q(register_1_q), .clk(clock_1_out), .clr(in_2));
  Clock clock_1 (.out(clock_1_out));
  // Probe on \累加中间结果 
  // ALU alu_1: pin names not known; wires that end beside it: multiplexer_1_out, register_1_q, 4'b0101, alu_1_p4
  assign \存入_读取地址  = not_1_out ? alu_1_p4[4:0] : 5'bz;  // Controlled_Buffer controlled_buffer_1
  Adder #(.width(5)) adder_1 (.a(alu_1_p4[4:0]), .b(5'b10000), .out(adder_1_out));  // open: cin, cout
  Comparator #(.width(32)) comparator_3 (.a(counter_1_q), .b(32'h11), .lt(comparator_3_lt));  // open: gt, eq
  assign \存入_读取地址  = clock_1_out ? adder_1_out : 5'bz;  // Controlled_Buffer controlled_buffer_2
  not not_1 (not_1_out, clock_1_out);
  RAM #(.addrWidth(5), .dataWidth(32), .bus("asynch")) ram_1 (
    .addr(\存入_读取地址 ), .data(ram_1_data), .sel(comparator_3_lt), .ld(not_1_out), .clr(in_1));
  assign ram_1_data = clock_1_out ? \累加中间结果  : 32'bz;  // Controlled_Buffer controlled_buffer_3
  assign \累加单项  = not_2_out ? ram_1_data : 32'bz;  // Controlled_Buffer controlled_buffer_4
  not not_2 (not_2_out, clock_1_out);
  Comparator #(.width(32)) comparator_4 (.a(counter_1_q), .b({32{1'b0}}), .gt(comparator_4_gt));  // open: eq, lt
  Hex_Digit_Display hex_digit_display_1 (.value(\累加中间结果 [27:24]));  // open: dp
  Hex_Digit_Display hex_digit_display_2 (.value(\累加中间结果 [31:28]));  // open: dp
  regfile regfile_1 (
    .Reg2(5'b00001), .Write_Reg_num(5'b00001), .Din(multiplexer_2_out), .Write_Enable(1'b1),
    .Clock(clock_1_out), .Reg2_2(\累加中间结果 ));  // open: Reg1_num, Reg1, s0_Value, s1_Value, s2_Value, ra_Value
  Multiplexer #(.width(32), .enable("false")) multiplexer_2 (
    .in0({32{1'b0}}), .in1(alu_2_p4), .out(multiplexer_2_out), .sel(comparator_4_gt));
  Hex_Digit_Display hex_digit_display_3 (.value(\累加中间结果 [23:20]));  // open: dp
  Hex_Digit_Display hex_digit_display_4 (.value(\累加中间结果 [19:16]));  // open: dp
  // ALU alu_2: pin names not known; wires that end beside it: \累加单项 , \累加中间结果 , 4'b0101, alu_2_p4
  Hex_Digit_Display hex_digit_display_5 (.value(\累加中间结果 [15:12]));  // open: dp
  Hex_Digit_Display hex_digit_display_6 (.value(\累加中间结果 [11:8]));  // open: dp
  Hex_Digit_Display hex_digit_display_7 (.value(\累加中间结果 [3:0]));  // open: dp
  Hex_Digit_Display hex_digit_display_8 (.value(\累加中间结果 [7:4]));  // open: dp
endmodule
